// Logisim project main.circ as structural Verilog: 3 circuits, main circuit main
module main (
  input  Reset
);

  wire decoder_1_out6, decoder_1_out7, LoadInstr;
  wire [2:0] rom_1_data;
  wire [4:0] addr, InstrAddr;

  instr_counter instr_counter_1 (.LoadAddress(LoadInstr), .AddressIn(addr), .reset(Reset), .AddressOut(InstrAddr));
  Decoder #(.select(3), .enable("false")) decoder_1 (
    .out6(decoder_1_out6), .out7(decoder_1_out7), .sel(rom_1_data));  // open: out0, out1, out2, out3, out4, out5
  or or_1 (LoadInstr, decoder_1_out7, decoder_1_out6);
  ROM #(.addrWidth(5)) rom_1 (.addr(InstrAddr), .data({rom_1_data, addr}), .sel(1'b1));

  // Other names for the same wires on the sheet: imm[3:0] = addr[3:0]; LoadAddr[4:0] = addr; offset[4:0] = addr;
  //   RFunc[2:0] = addr[2:0]; rx = addr[3]; rd = addr[4]
endmodule

// RAM
module RAM_module (
  input  [7:0] DataIn,
  input  [7:0] Address,
  input  Reset,
  input  MemWrite,
  output [7:0] DataOut
);

  wire clock_1_out, not_1_out;

  Clock clock_1 (.out(clock_1_out));
  not not_1 (not_1_out, MemWrite);
  assign DataOut = MemWrite ? DataIn : 8'bz;  // Controlled_Buffer controlled_buffer_1
  RAM ram_1 (.addr(Address), .data(DataOut), .sel(1'b1), .clk(clock_1_out), .ld(not_1_out), .clr(Reset));
endmodule

// IC
module instr_counter (
  input  LoadAddress,
  input  [4:0] AddressIn,
  input  reset,
  output [4:0] AddressOut
);

  wire clock_1_out, not_1_out;

  not not_1 (not_1_out, LoadAddress);
  Counter #(.width(5), .max('h1f), .ongoal("stay")) counter_1 (
    .load(LoadAddress), .D(AddressIn), .count(not_1_out), .Q(AddressOut), .clk(clock_1_out), .clr(reset));  // open: carry
  Clock clock_1 (.out(clock_1_out));
endmodule
